// Logisim project Ula.circ as structural Verilog
module ULA (
  input  [7:0] A,
  input  [7:0] B,
  input  [2:0] \Operação ,
  input  Clock,
  input  [2:0] Desloca,
  input  Clear,
  output [7:0] SAIDA,
  output OverFlow
);

  wire decodificador_1_c0, decodificador_1_c1, decodificador_1_c2, decodificador_1_c3, decodificador_1_c4,
       decodificador_1_c5, decodificador_1_c6, decodificador_1_c7;

  \Cód_000__AND  \cód_000_and_1  (.A(A), .B(B), .out_4(SAIDA), .Habilita(decodificador_1_c0));
  \Cód_001__OR  \cód_001_or_1  (.A(A), .B(B), .out_4(SAIDA), .Habilitar(decodificador_1_c4));
  DECODIFICADOR decodificador_1 (
    .C0(decodificador_1_c0), .C1(decodificador_1_c1), .C2(decodificador_1_c2), .C3(decodificador_1_c3),
    .C4(decodificador_1_c4), .C5(decodificador_1_c5), .C6(decodificador_1_c6), .C7(decodificador_1_c7),
    .A(\Operação [0]), .B(\Operação [1]), .C(\Operação [2]));
  \Cód_010___SOMADOR  \cód_010_somador_1  (
    .A(A), .B(B), .Cout(OverFlow), .Saida(SAIDA), .Habilitar(decodificador_1_c2));
  \Cód_011__COMPARAÇÃO  \cód_011_comparação_1  ();
  \Cód_100__SUBTRAÇÃO  \cód_100_subtração_1  (
    .out_4(SAIDA), .A(A), .B(B), .Habilitar(decodificador_1_c1));  // open: BorrowOut
  \Cód_101__MULTIPLICADOR  \cód_101_multiplicador_1  (
    .B(B), .A(A), .desloca(Desloca), .Clear(Clear), .Habilitar(decodificador_1_c5), .Resultado(SAIDA),
    .Clock(Clock));  // open: OverFlow, out_8
  \Cód_110__COPIA_DO_1_OPERANDO  \cód_110_copia_do_1_operando_1  (.Habilitar(decodificador_1_c3), .out_3(SAIDA), .A(A));
  \Cód_111__COPIA_DO_2_OPERANDO  \cód_111_copia_do_2_operando_1  (.Habilitar(decodificador_1_c7), .out_3(SAIDA), .B(B));
endmodule

// AND
module \Cód_000__AND  (
  input  [7:0] A,
  input  [7:0] B,
  input  Habilita,
  output [7:0] out_4
);

  wire [7:0] and_1_out;

  assign and_1_out = A & B;  // AND_Gate and_1, 8 bits wide
  assign out_4 = Habilita ? and_1_out : 8'bz;  // Controlled_Buffer controlled_buffer_1
endmodule

// OR
module \Cód_001__OR  (
  input  [7:0] A,
  input  [7:0] B,
  input  Habilitar,
  output [7:0] out_4
);

  wire [7:0] or_1_out;

  assign or_1_out = A | B;  // OR_Gate or_1, 8 bits wide
  assign out_4 = Habilitar ? or_1_out : 8'bz;  // Controlled_Buffer controlled_buffer_1
endmodule

// soma
module \Cód_010___SOMADOR  (
  input  [7:0] A,
  input  [7:0] B,
  input  Habilitar,
  output [7:0] Saida,
  output Cout
);

  wire somabits_1_cout, somabits_2_cout, somabits_3_cout, somabits_4_cout, somabits_5_cout, somabits_6_cout,
       somabits_7_cout;
  wire [7:0] \somabits_1_saída ;

  SomaBits somabits_1 (.\Saída (\somabits_1_saída [0]), .Cout(somabits_1_cout), .B(A[0]), .A(1'b0), .Cin(B[0]));
  SomaBits somabits_2 (
    .\Saída (\somabits_1_saída [1]), .Cout(somabits_2_cout), .B(A[1]), .A(somabits_1_cout), .Cin(B[1]));
  SomaBits somabits_3 (
    .\Saída (\somabits_1_saída [2]), .Cout(somabits_3_cout), .B(A[2]), .A(somabits_2_cout), .Cin(B[2]));
  SomaBits somabits_4 (
    .\Saída (\somabits_1_saída [3]), .Cout(somabits_4_cout), .B(A[3]), .A(somabits_3_cout), .Cin(B[3]));
  SomaBits somabits_5 (
    .\Saída (\somabits_1_saída [4]), .Cout(somabits_5_cout), .B(A[4]), .A(somabits_4_cout), .Cin(B[4]));
  SomaBits somabits_6 (
    .\Saída (\somabits_1_saída [5]), .Cout(somabits_6_cout), .B(A[5]), .A(somabits_5_cout), .Cin(B[5]));
  SomaBits somabits_7 (
    .\Saída (\somabits_1_saída [6]), .Cout(somabits_7_cout), .B(A[6]), .A(somabits_6_cout), .Cin(B[6]));
  SomaBits somabits_8 (.\Saída (\somabits_1_saída [7]), .Cout(Cout), .B(A[7]), .A(somabits_7_cout), .Cin(B[7]));
  assign Saida = Habilitar ? \somabits_1_saída  : 8'bz;  // Controlled_Buffer controlled_buffer_1
endmodule

// Subtraçao
module \Cód_100__SUBTRAÇÃO  (
  input  [7:0] A,
  input  [7:0] B,
  input  Habilitar,
  output [7:0] out_4,
  output BorrowOut
);

  wire \subtraçãobits_1_bout , \subtraçãobits_2_bout , \subtraçãobits_3_bout , \subtraçãobits_4_bout ,
       \subtraçãobits_5_bout , \subtraçãobits_6_bout , \subtraçãobits_7_bout ;
  wire [7:0] \subtraçãobits_1_saida ;

  \subtraçãoBits  \subtraçãobits_1  (
    .A(A[0]), .Saida(\subtraçãobits_1_saida [0]), .B(B[0]), .BOut(\subtraçãobits_1_bout ), .Bin(1'b0));
  \subtraçãoBits  \subtraçãobits_2  (
    .A(A[1]), .Saida(\subtraçãobits_1_saida [1]), .B(B[1]), .BOut(\subtraçãobits_2_bout ),
    .Bin(\subtraçãobits_1_bout ));
  \subtraçãoBits  \subtraçãobits_3  (
    .A(A[2]), .Saida(\subtraçãobits_1_saida [2]), .B(B[2]), .BOut(\subtraçãobits_3_bout ),
    .Bin(\subtraçãobits_2_bout ));
  \subtraçãoBits  \subtraçãobits_4  (
    .A(A[3]), .Saida(\subtraçãobits_1_saida [3]), .B(B[3]), .BOut(\subtraçãobits_4_bout ),
    .Bin(\subtraçãobits_3_bout ));
  \subtraçãoBits  \subtraçãobits_5  (
    .A(A[4]), .Saida(\subtraçãobits_1_saida [4]), .B(B[4]), .BOut(\subtraçãobits_5_bout ),
    .Bin(\subtraçãobits_4_bout ));
  \subtraçãoBits  \subtraçãobits_6  (
    .A(A[5]), .Saida(\subtraçãobits_1_saida [5]), .B(B[5]), .BOut(\subtraçãobits_6_bout ),
    .Bin(\subtraçãobits_5_bout ));
  \subtraçãoBits  \subtraçãobits_7  (
    .A(A[6]), .Saida(\subtraçãobits_1_saida [6]), .B(B[6]), .BOut(\subtraçãobits_7_bout ),
    .Bin(\subtraçãobits_6_bout ));
  \subtraçãoBits  \subtraçãobits_8  (
    .A(A[7]), .Saida(\subtraçãobits_1_saida [7]), .B(B[7]), .BOut(BorrowOut), .Bin(\subtraçãobits_7_bout ));
  assign out_4 = Habilitar ? \subtraçãobits_1_saida  : 8'bz;  // Controlled_Buffer controlled_buffer_1
endmodule

// Resultado
module \Cód_101__MULTIPLICADOR  (
  input  [7:0] B,
  input  [7:0] A,
  input  Clock,
  input  [2:0] desloca,
  input  Clear,
  input  Habilitar,
  output OverFlow,
  output [7:0] out_8,
  output [7:0] Resultado
);

  wire and_9_out, multiplexador_1_out_12, not_1_out, not_2_out;
  wire [2:0] contador_1__1;
  wire [7:0] and_1_out, \cód_110_copia_do_1_operando_1_out_3 , d_ff_1_q, d_ff_8_q, shifter_1_out;

  D_Flip_Flop d_ff_1 (
    .clk(not_2_out), .D(\cód_110_copia_do_1_operando_1_out_3 [0]), .Q(d_ff_1_q[0]), .reset(Clear));  // open: Qn, preset, en
  contador contador_1 (.Clock(Clock), ._1(contador_1__1[2]), ._3(contador_1__1[1]), ._2(contador_1__1[0]));
  D_Flip_Flop d_ff_2 (
    .clk(not_2_out), .D(\cód_110_copia_do_1_operando_1_out_3 [1]), .Q(d_ff_1_q[1]), .reset(Clear));  // open: Qn, preset, en
  D_Flip_Flop d_ff_3 (
    .clk(not_2_out), .D(\cód_110_copia_do_1_operando_1_out_3 [2]), .Q(d_ff_1_q[2]), .reset(Clear));  // open: Qn, preset, en
  D_Flip_Flop d_ff_4 (
    .clk(not_2_out), .D(\cód_110_copia_do_1_operando_1_out_3 [3]), .Q(d_ff_1_q[3]), .reset(Clear));  // open: Qn, preset, en
  D_Flip_Flop d_ff_5 (
    .clk(not_2_out), .D(\cód_110_copia_do_1_operando_1_out_3 [4]), .Q(d_ff_1_q[4]), .reset(Clear));  // open: Qn, preset, en
  Multiplexador multiplexador_1 (
    .D0(B[0]), .D1(B[1]), .D2(B[2]), .D3(B[3]), .D4(B[4]), .D5(B[5]), .D6(B[6]), .D7(B[7]),
    .A(contador_1__1[2]), .B(contador_1__1[1]), .C(contador_1__1[0]), .out_12(multiplexador_1_out_12));
  and and_1 (and_1_out[0], A[0], multiplexador_1_out_12);
  D_Flip_Flop d_ff_6 (
    .clk(not_2_out), .D(\cód_110_copia_do_1_operando_1_out_3 [6]), .Q(d_ff_1_q[6]), .reset(Clear));  // open: Qn, preset, en
  D_Flip_Flop d_ff_7 (
    .clk(not_2_out), .D(\cód_110_copia_do_1_operando_1_out_3 [5]), .Q(d_ff_1_q[5]), .reset(Clear));  // open: Qn, preset, en
  and and_2 (and_1_out[1], A[1], multiplexador_1_out_12);
  D_Flip_Flop d_ff_8 (.clk(Clock), .D(shifter_1_out[0]), .Q(d_ff_8_q[0]));  // open: Qn, preset, en, reset
  D_Flip_Flop d_ff_9 (
    .clk(not_2_out), .D(\cód_110_copia_do_1_operando_1_out_3 [7]), .Q(d_ff_1_q[7]), .reset(Clear));  // open: Qn, preset, en
  \Cód_110__COPIA_DO_1_OPERANDO  \cód_110_copia_do_1_operando_1  (
    .Habilitar(Habilitar), .out_3(\cód_110_copia_do_1_operando_1_out_3 ), .A(out_8));
  and and_3 (and_1_out[2], A[2], multiplexador_1_out_12);
  and and_4 (and_1_out[3], A[3], multiplexador_1_out_12);
  D_Flip_Flop d_ff_10 (.clk(Clock), .D(shifter_1_out[1]), .Q(d_ff_8_q[1]));  // open: Qn, preset, en, reset
  and and_5 (and_1_out[4], A[4], multiplexador_1_out_12);
  D_Flip_Flop d_ff_11 (.clk(Clock), .D(shifter_1_out[2]), .Q(d_ff_8_q[2]));  // open: Qn, preset, en, reset
  and and_6 (and_1_out[5], A[5], multiplexador_1_out_12);
  Shifter shifter_1 (.in(and_1_out), .\dist (desloca), .out(shifter_1_out));
  D_Flip_Flop d_ff_12 (.clk(Clock), .D(shifter_1_out[3]), .Q(d_ff_8_q[3]));  // open: Qn, preset, en, reset
  \Cód_010___SOMADOR  \cód_010_somador_1  (
    .A(d_ff_8_q), .B(d_ff_1_q), .Cout(OverFlow), .Saida(out_8), .Habilitar(Habilitar));
  and and_7 (and_1_out[6], A[6], multiplexador_1_out_12);
  and and_8 (and_1_out[7], A[7], multiplexador_1_out_12);
  D_Flip_Flop d_ff_13 (.clk(Clock), .D(shifter_1_out[4]), .Q(d_ff_8_q[4]));  // open: Qn, preset, en, reset
  D_Flip_Flop d_ff_14 (.clk(Clock), .D(shifter_1_out[5]), .Q(d_ff_8_q[5]));  // open: Qn, preset, en, reset
  assign Resultado = and_9_out ? out_8 : 8'bz;  // Controlled_Buffer controlled_buffer_1
  not not_1 (not_1_out, contador_1__1[1]);
  D_Flip_Flop d_ff_15 (.clk(Clock), .D(shifter_1_out[6]), .Q(d_ff_8_q[6]));  // open: Qn, preset, en, reset
  D_Flip_Flop d_ff_16 (.clk(Clock), .D(shifter_1_out[7]), .Q(d_ff_8_q[7]));  // open: Qn, preset, en, reset
  not not_2 (not_2_out, Clock);
  and and_9 (and_9_out, Habilitar, contador_1__1[0], not_1_out, contador_1__1[2]);
endmodule

// copia de A
module \Cód_110__COPIA_DO_1_OPERANDO  (
  input  [7:0] A,
  input  Habilitar,
  output [7:0] out_3
);

  assign out_3 = Habilitar ? A : 8'bz;  // Controlled_Buffer controlled_buffer_1
endmodule

// Copia B
module \Cód_111__COPIA_DO_2_OPERANDO  (
  input  [7:0] B,
  input  Habilitar,
  output [7:0] out_3
);

  assign out_3 = Habilitar ? B : 8'bz;  // Controlled_Buffer controlled_buffer_1
endmodule

module \subtraçãoBits  (
  input  A,
  input  B,
  input  Bin,
  output Saida,
  output BOut
);

  wire and_1_out, and_2_out, and_3_out, not_1_out, or_1_out, xor_1_out;

  not not_1 (not_1_out, A);
  xor xor_1 (xor_1_out, A, B);
  and and_1 (and_1_out, not_1_out, B);
  or or_1 (or_1_out, and_1_out, and_2_out);
  and and_2 (and_2_out, not_1_out, Bin);
  and and_3 (and_3_out, Bin, B);
  xor xor_2 (Saida, xor_1_out, Bin);
  or or_2 (BOut, or_1_out, and_3_out);
endmodule

// Decodificador
module DECODIFICADOR (
  input  A,
  input  B,
  input  C,
  output C0,
  output C1,
  output C2,
  output C3,
  output C4,
  output C5,
  output C6,
  output C7
);

  wire not_1_out, not_2_out, not_3_out, not_4_out, not_5_out, not_6_out, not_7_out, not_8_out, not_9_out,
       not_10_out, not_11_out, not_12_out;

  not not_1 (not_1_out, A);
  not not_2 (not_2_out, B);
  not not_3 (not_3_out, C);
  not not_4 (not_4_out, A);
  not not_5 (not_5_out, B);
  not not_6 (not_6_out, A);
  not not_7 (not_7_out, C);
  not not_8 (not_8_out, A);
  not not_9 (not_9_out, B);
  not not_10 (not_10_out, C);
  not not_11 (not_11_out, B);
  not not_12 (not_12_out, C);
  and and_1 (C7, A, B, C);
  and and_2 (C0, not_1_out, not_2_out, not_3_out);
  and and_3 (C1, not_4_out, not_5_out, C);
  and and_4 (C2, not_6_out, B, not_7_out);
  and and_5 (C3, not_8_out, B, C);
  and and_6 (C4, A, not_9_out, not_10_out);
  and and_7 (C5, A, not_11_out, C);
  and and_8 (C6, A, B, not_12_out);
endmodule

module SomaBits (
  input  Cin,
  input  B,
  input  A,
  output \Saída ,
  output Cout
);

  wire and_1_out, and_2_out, xor_1_out;

  xor xor_1 (xor_1_out, A, B);
  and and_1 (and_1_out, A, B);
  xor xor_2 (\Saída , Cin, xor_1_out);
  and and_2 (and_2_out, Cin, xor_1_out);
  or or_1 (Cout, and_1_out, and_2_out);
endmodule

module Deslocador (
  input  D2,
  input  D3,
  input  D4,
  input  D5,
  input  D6,
  input  D7,
  input  D0,
  input  D1,
  input  C,
  output out_10,
  output out_11,
  output out_12,
  output out_13,
  output out_14,
  output out_15,
  output out_16,
  output out_17
);

  wire and_1_out, and_2_out, and_4_out, and_5_out, and_6_out, and_7_out, and_8_out, and_9_out, and_10_out,
       and_11_out, and_12_out, and_14_out, not_1_out;

  not not_1 (not_1_out, C);
  and and_1 (and_1_out, D0, C);
  and and_2 (and_2_out, D1, C);
  and and_3 (out_11, not_1_out, D1);
  or or_1 (out_10, and_1_out, and_5_out);
  and and_4 (and_4_out, D2, C);
  and and_5 (and_5_out, not_1_out, D2);
  or or_2 (out_12, and_2_out, and_6_out);
  and and_6 (and_6_out, not_1_out, D3);
  or or_3 (out_13, and_4_out, and_7_out);
  and and_7 (and_7_out, not_1_out, D4);
  and and_8 (and_8_out, D3, C);
  and and_9 (and_9_out, D4, C);
  or or_4 (out_14, and_8_out, and_10_out);
  and and_10 (and_10_out, not_1_out, D5);
  and and_11 (and_11_out, D5, C);
  or or_5 (out_15, and_9_out, and_12_out);
  and and_12 (and_12_out, not_1_out, D6);
  or or_6 (out_16, and_11_out, and_14_out);
  and and_13 (out_17, D6, C);
  and and_14 (and_14_out, not_1_out, D7);
endmodule

module Multiplexador (
  input  D0,
  input  D1,
  input  D2,
  input  D3,
  input  D4,
  input  D5,
  input  D6,
  input  D7,
  input  A,
  input  B,
  input  C,
  output out_12
);

  wire and_1_out, and_2_out, and_3_out, and_4_out, and_5_out, and_6_out, and_7_out, and_8_out, not_1_out,
       not_2_out, not_3_out;

  not not_1 (not_1_out, A);
  not not_2 (not_2_out, B);
  not not_3 (not_3_out, C);
  and and_1 (and_1_out, D0, not_1_out, not_2_out, not_3_out);
  and and_2 (and_2_out, D1, not_1_out, not_2_out, C);
  and and_3 (and_3_out, D2, not_1_out, B, not_3_out);
  and and_4 (and_4_out, D3, not_1_out, B, C);
  and and_5 (and_5_out, D4, A, not_2_out, not_3_out);
  and and_6 (and_6_out, D5, A, not_2_out, C);
  and and_7 (and_7_out, D6, A, B, not_3_out);
  and and_8 (and_8_out, D7, A, B, C);
  or or_1 (out_12, and_1_out, and_2_out, and_3_out, and_4_out, and_5_out, and_6_out, and_7_out, and_8_out);
endmodule

module contador (
  input  Clock,
  output _1,
  output _3,
  output _2
);

  wire d_ff_1_qn, d_ff_2_qn, d_ff_3_qn;

  D_Flip_Flop d_ff_1 (.clk(Clock), .D(d_ff_1_qn), .Q(_1), .Qn(d_ff_1_qn));  // open: preset, en, reset
  D_Flip_Flop d_ff_2 (.clk(d_ff_1_qn), .D(d_ff_2_qn), .Q(_2), .Qn(d_ff_2_qn));  // open: preset, en, reset
  D_Flip_Flop d_ff_3 (.clk(d_ff_2_qn), .D(d_ff_3_qn), .Q(_3), .Qn(d_ff_3_qn));  // open: preset, en, reset
endmodule

module Complemento (
  input  [7:0] Saida,
  input  [7:0] A,
  input  Habilita,
  output OverFlow
);

  wire [7:0] \cód_010_somador_1_saida , not_1_out;

  assign not_1_out = ~A;  // NOT_Gate not_1, 8 bits wide
  \Cód_010___SOMADOR  \cód_010_somador_1  (
    .A(not_1_out), .B(8'h1), .Cout(OverFlow), .Saida(\cód_010_somador_1_saida ), .Habilitar(1'b1));
  assign Saida = Habilita ? \cód_010_somador_1_saida  : 8'bz;  // Controlled_Buffer controlled_buffer_1
endmodule
